# Fritzing sketch schematic (saved by Fritzing 0.9.9b)

parts:
  Bat1 = battery_holder_single_18650
  Bat2 = battery_holder_single_18650
  Bat3 = battery_holder_single_18650
  Mod1 = 3S-BMS
  U1 = DC-DC 2-24V Step Up Booster [package=THT]
  J1 = Power Jack [package=power_jack_pth]
  J2 = Power Jack [package=power_jack_pth]
  D1 = Rectifier Diode [part_number=1N4001 package="Melf DO-213 AB [SMD]"]
  M1 = volt-ammeter [package=THT]
  S1 = SWITCH-MOMENTARY-2 [package=tactile-pth-12mm]

nets:
  N1: Bat1.+#0, Bat2.+#1, Mod1.8.4V
  N2: Bat1.+#1, Mod1.12.6V
  N3: Bat2.+#0, Bat3.+#1, Mod1.4.2V
  N4: Bat3.+#0, Mod1.0V
  N5: Mod1.-, U1.pin4, J2.GND, M1.-PWR, M1.-LOAD, M1.Meter_-
  N6: Mod1.+, U1.pin3, D1.cathode, S1.1
  N7: U1.pin1, J1.PWR
  N8: U1.pin2, J1.GND
  N9: J2.PWR, D1.anode
  N10: M1.LOAD_V+, M1.Meter_+, S1.2

custom parts:
  battery_holder_single_18650: single 18650 battery holder
  3S-BMS: 3S-BMS LIPO battery charger / protection unit. Note pcb does not match the board as it will likely connect with wires, so pcb is 6 pads suitable for .1in header pins.
  DC-DC 2-24V Step Up Booster: Convertisseur DC-DC 2-24V 2A
  volt-ammeter: Volt-ammeter 0-100V 0-10A panel mount.
